# Fritzing sketch Launometer (saved by Fritzing 0.8.5b)
breadboards: 1

parts:
  IC1 = IC, DIP package, 18 pins [chip_label=LM3915]
  LED1 = LED - 5mm [color="Red (633nm)" package="5 mm [THT]"]
  LED2 = LED - 5mm [color="Red (633nm)" package="5 mm [THT]"]
  LED3 = LED - 5mm [color="Red (633nm)" package="5 mm [THT]"]
  LED4 = LED - 5mm [color="Yellow (585nm)" package="5 mm [THT]"]
  LED5 = LED - 5mm [color="Yellow (585nm)" package="5 mm [THT]"]
  LED6 = LED - 5mm [color="Yellow (585nm)" package="5 mm [THT]"]
  LED7 = LED - 5mm [color="Green (565nm)" package="5 mm [THT]"]
  LED8 = LED - 5mm [color="Green (565nm)" package="5 mm [THT]"]
  LED9 = LED - 5mm [color="Green (565nm)" package="5 mm [THT]"]
  R1 = Resistor [tolerance=±5% resistance=1.5k package=THT]
  S1 = Pushbutton [package="[THT]"]
  R2 = Resistor [tolerance=±1% resistance=3.3k package=THT]
  R3 = Rotary Potentiometer (Small) [maximum_resistance=10kΩ package=THT]
  VCC1 = Battery

nets:
  N1: IC1.pin2, IC1.pin4, R2.Pin_0, R3.leg2, VCC1.-
  N2: IC1.pin3, S1.Pin_3, S1.Pin_4, R3.leg1, VCC1.+
  N3: IC1.pin5, R3.wiper
  N4: IC1.pin6, IC1.pin7, R1.Pin_0
  N5: IC1.pin8, R1.Pin_1, R2.Pin_1
  N6: IC1.pin10, LED9.cathode
  N7: IC1.pin11, LED8.cathode
  N8: IC1.pin12, LED7.cathode
  N9: IC1.pin13, LED6.cathode
  N10: IC1.pin14, LED5.cathode
  N11: IC1.pin15, LED4.cathode
  N12: IC1.pin16, LED3.cathode
  N13: IC1.pin17, LED2.cathode
  N14: IC1.pin18, LED1.cathode
  N15: LED1.anode, LED2.anode, LED3.anode, LED4.anode, LED5.anode, LED6.anode, LED7.anode, LED8.anode, LED9.anode, S1.Pin_1, S1.Pin_2
